// Logisim project ProyectoMIPS.circ as structural Verilog: 15 circuits, main circuit main
// address
module main (
  input  Active_Store,
  output [1:0] out_2,
  output [3:0] out_3
);

  wire adder_2_cout, ALUSrc, and_1_out, Branch, clock, Jump, letter_1_out_2, letter_1_out_3, letter_1_out_4,
       letter_1_out_5, letter_1_out_6, letter_1_out_7, letter_1_out_8, letter_2_out_2, letter_2_out_3,
       letter_2_out_4, letter_2_out_5, letter_2_out_6, letter_2_out_7, letter_2_out_8, letter_3_out_2,
       letter_3_out_3, letter_3_out_4, letter_3_out_5, letter_3_out_6, letter_3_out_7, letter_3_out_8,
       MemRead, MemToReg, MemToWrite, not_1_out, num_1_out_2, num_1_out_3, num_1_out_4, num_1_out_5,
       num_1_out_6, num_1_out_7, num_1_out_8, num_2_out_2, num_2_out_3, num_2_out_4, num_2_out_5,
       num_2_out_6, num_2_out_7, num_2_out_8, num_3_out_2, num_3_out_3, num_3_out_4, num_3_out_5,
       num_3_out_6, num_3_out_7, num_3_out_8, num_4_out_2, num_4_out_3, num_4_out_4, num_4_out_5,
       num_4_out_6, num_4_out_7, num_4_out_8, num_5_out_2, num_5_out_3, num_5_out_4, num_5_out_5,
       num_5_out_6, num_5_out_7, num_5_out_8, num_6_out_2, num_6_out_3, num_6_out_4, num_6_out_5,
       num_6_out_6, num_6_out_7, num_6_out_8, num_7_out_2, num_7_out_3, num_7_out_4, num_7_out_5,
       num_7_out_6, num_7_out_7, num_7_out_8, num_8_out_2, num_8_out_3, num_8_out_4, num_8_out_5,
       num_8_out_6, num_8_out_7, num_8_out_8, num_9_out_2, num_9_out_3, num_9_out_4, num_9_out_5,
       num_9_out_6, num_9_out_7, num_9_out_8, num_10_out_2, num_10_out_3, num_10_out_4, num_10_out_5,
       num_10_out_6, num_10_out_7, num_10_out_8, num_11_out_2, num_11_out_3, num_11_out_4, num_11_out_5,
       num_11_out_6, num_11_out_7, num_11_out_8, num_12_out_2, num_12_out_3, num_12_out_4, num_12_out_5,
       num_12_out_6, num_12_out_7, num_12_out_8, num_13_out_2, num_13_out_3, num_13_out_4, num_13_out_5,
       num_13_out_6, num_13_out_7, num_13_out_8, num_14_out_2, num_14_out_3, num_14_out_4, num_14_out_5,
       num_14_out_6, num_14_out_7, num_14_out_8, num_15_out_2, num_15_out_3, num_15_out_4, num_15_out_5,
       num_15_out_6, num_15_out_7, num_15_out_8, rd0, rd1, rd2, rd3, rd4, RegDst, RegWrite, Reset_2_out,
       Reset_3_out, Reset_4_out, Reset_out, rs0, rs1, rs2, rs3, rs4, rt0, rt1, rt2, rt3, rt4, Zero;
  wire [3:0] bit_extender_5_out;
  wire [4:0] multiplexer_3_out, rd, rs, rt;
  wire [5:0] decode_1_dibujado, funct, Opcode;
  wire [6:0] s1, s2, s3;
  wire [15:0] address;
  wire [23:0] adder_1_out, adder_2_out, bit_extender_1_out, bit_extender_2_out, bit_extender_4_out,
       multiplexer_2_out, multiplexer_4_out, PcInc, register_1_q, subtractor_1_out;
  wire [25:0] addressJ;
  wire [31:0] addressExtend, alu_1_aluresult, multiplexer_1_out, ram_1_data, ram_2_data, ReadData2,
       register_2_readdata1, WriteData;

  Button Reset (.out(Reset_out));
  Penilla penilla_1 (.Input(rs), .s0(rs0), .s1(rs1), .s2(rs2), .s3(rs3), .s4(rs4));
  Penilla penilla_2 (.Input(rt), .s0(rt0), .s1(rt1), .s2(rt2), .s3(rt3), .s4(rt4));
  Penilla penilla_3 (.Input(rd), .s0(rd0), .s1(rd1), .s2(rd2), .s3(rd3), .s4(rd4));
  Adder #(.width(24)) adder_1 (.a(register_1_q), .b(24'h1), .out(adder_1_out));  // open: cin, cout
  Register_part #(.width(24)) register_1 (.D(PcInc), .Q(register_1_q), .clk(clock), .clr(Reset_out));  // open: en
  _7_Segment_Display u_7_segment_display_1 (
    .g(letter_1_out_5), .f(letter_1_out_4), .a(letter_1_out_3), .b(letter_1_out_2), .e(letter_1_out_8),
    .d(letter_1_out_7), .c(letter_1_out_6));  // open: dp
  Letter letter_1 (
    .Number(s1), .out_8(letter_1_out_8), .out_7(letter_1_out_7), .out_6(letter_1_out_6),
    .out_5(letter_1_out_5), .out_4(letter_1_out_4), .out_3(letter_1_out_3), .out_2(letter_1_out_2));
  _7_Segment_Display u_7_segment_display_2 (
    .g(letter_2_out_5), .f(letter_2_out_4), .a(letter_2_out_3), .b(letter_2_out_2), .e(letter_2_out_8),
    .d(letter_2_out_7), .c(letter_2_out_6));  // open: dp
  Letter letter_2 (
    .Number(s2), .out_8(letter_2_out_8), .out_7(letter_2_out_7), .out_6(letter_2_out_6),
    .out_5(letter_2_out_5), .out_4(letter_2_out_4), .out_3(letter_2_out_3), .out_2(letter_2_out_2));
  Bit_Extender #(.in_width(26), .out_width(24)) bit_extender_1 (.in(addressJ), .out(bit_extender_1_out));
  assign bit_extender_2_out = {{9{1'b0}}, address[14:0]};  // Bit_Extender bit_extender_2
  RAM #(.addrWidth(24), .dataWidth(32), .bus("separate")) ram_1 (
    .addr(register_1_q), .data(ram_1_data), .str(Active_Store), .clk(clock), .ld(1'b1), .clr(Reset_2_out));  // open: din, sel
  Button Reset_2 (.out(Reset_2_out));
  _7_Segment_Display u_7_segment_display_3 (
    .g(letter_3_out_5), .f(letter_3_out_4), .a(letter_3_out_3), .b(letter_3_out_2), .e(letter_3_out_8),
    .d(letter_3_out_7), .c(letter_3_out_6));  // open: dp
  Letter letter_3 (
    .Number(s3), .out_8(letter_3_out_8), .out_7(letter_3_out_7), .out_6(letter_3_out_6),
    .out_5(letter_3_out_5), .out_4(letter_3_out_4), .out_3(letter_3_out_3), .out_2(letter_3_out_2));
  assign addressExtend = {{16{1'b0}}, address};  // Bit_Extender bit_extender_3
  Adder #(.width(24)) adder_2 (
    .a(adder_1_out), .b(bit_extender_2_out), .out(adder_2_out), .cout(adder_2_cout));  // open: cin
  Subtractor #(.width(24)) subtractor_1 (
    .a(adder_1_out), .b(bit_extender_2_out), .out(subtractor_1_out), .bin(adder_2_cout));  // open: bout
  Decode decode_1 (
    .in_1(ram_1_data), .Address_J(addressJ), .Address(address), .rs(rs), .rt(rt), .rd(rd),
    .Dibujado(decode_1_dibujado), .funct(funct), .Op(Opcode));  // open: Shamt
  ShowOp_funct showop_funct_1 (.Funct_0p(decode_1_dibujado), .s1(s1), .s2(s2), .s2_2(s3));
  Multiplexer #(.width(32), .enable("false")) multiplexer_1 (
    .in0(ReadData2), .in1(addressExtend), .out(multiplexer_1_out), .sel(ALUSrc));
  Multiplexer #(.width(24), .enable("false")) multiplexer_2 (
    .in0(adder_2_out), .in1(subtractor_1_out), .out(multiplexer_2_out), .sel(address[15]));
  Clock clock_1 (.out(clock));
  Multiplexer #(.width(5), .enable("false")) multiplexer_3 (.in0(rt), .in1(rd), .out(multiplexer_3_out), .sel(RegDst));
  Multiplexer #(.width(24), .enable("false")) multiplexer_4 (
    .in0(adder_1_out), .in1(multiplexer_2_out), .out(multiplexer_4_out), .sel(and_1_out));
  Register register_2 (
    .ReadRegister1(rs), .WriteData(WriteData), .ReadRegister2(rt), .WriteRegister(multiplexer_3_out),
    .RegWrite(RegWrite), .ReadData1(register_2_readdata1), .ReadData2(ReadData2), .Clock(clock),
    .Reset(Reset_3_out));
  Button Reset_3 (.out(Reset_3_out));
  ALU_Control alu_control_1 (.ALUop(out_2), .funct(funct), .AluControlOutput(out_3));
  Multiplexer #(.width(24), .enable("false")) multiplexer_5 (
    .in0(bit_extender_1_out), .in1(multiplexer_4_out), .out(PcInc), .sel(not_1_out));
  not not_1 (not_1_out, Jump);
  and and_1 (and_1_out, Zero, Branch);
  Unidad_de_Control unidad_de_control_1 (
    .OpCode(Opcode), .RegDst(RegDst), .Branch(Branch), .MemRead(MemRead), .MemToReg(MemToReg), .ALUop(out_2),
    .MemWrite(MemToWrite), .ALUSrc(ALUSrc), .Regwrite(RegWrite), .Jump(Jump));
  ALU alu_1 (
    .Dato1(register_2_readdata1), .Dato2(multiplexer_1_out), .ALUResult(alu_1_aluresult), .ALUop(out_3),
    .Zero(Zero));
  Bit_Extender #(.in_width(32), .out_width(24)) bit_extender_4 (.in(alu_1_aluresult), .out(bit_extender_4_out));
  Button Reset_4 (.out(Reset_4_out));
  Multiplexer #(.width(32), .enable("false")) multiplexer_6 (
    .in0(alu_1_aluresult), .in1(ram_2_data), .out(WriteData), .sel(MemToReg));
  RAM #(.addrWidth(24), .dataWidth(32), .bus("separate")) ram_2 (
    .addr(bit_extender_4_out), .din(ReadData2), .data(ram_2_data), .str(MemToWrite), .clk(clock),
    .ld(MemRead), .clr(Reset_4_out));  // open: sel
  _7_Segment_Display u_7_segment_display_4 (
    .g(num_1_out_5), .f(num_1_out_4), .a(num_1_out_3), .b(num_1_out_2), .e(num_1_out_8), .d(num_1_out_7),
    .c(num_1_out_6));  // open: dp
  num num_1 (
    .in_1(rs4), .out_8(num_1_out_8), .out_7(num_1_out_7), .out_6(num_1_out_6), .out_5(num_1_out_5),
    .out_4(num_1_out_4), .out_3(num_1_out_3), .out_2(num_1_out_2));
  _7_Segment_Display u_7_segment_display_5 (
    .g(num_2_out_5), .f(num_2_out_4), .a(num_2_out_3), .b(num_2_out_2), .e(num_2_out_8), .d(num_2_out_7),
    .c(num_2_out_6));  // open: dp
  num num_2 (
    .in_1(rt4), .out_8(num_2_out_8), .out_7(num_2_out_7), .out_6(num_2_out_6), .out_5(num_2_out_5),
    .out_4(num_2_out_4), .out_3(num_2_out_3), .out_2(num_2_out_2));
  _7_Segment_Display u_7_segment_display_6 (
    .g(num_3_out_5), .f(num_3_out_4), .a(num_3_out_3), .b(num_3_out_2), .e(num_3_out_8), .d(num_3_out_7),
    .c(num_3_out_6));  // open: dp
  num num_3 (
    .in_1(rd4), .out_8(num_3_out_8), .out_7(num_3_out_7), .out_6(num_3_out_6), .out_5(num_3_out_5),
    .out_4(num_3_out_4), .out_3(num_3_out_3), .out_2(num_3_out_2));
  // Probe on ram_2_data
  _7_Segment_Display u_7_segment_display_7 (
    .g(num_4_out_5), .f(num_4_out_4), .a(num_4_out_3), .b(num_4_out_2), .e(num_4_out_8), .d(num_4_out_7),
    .c(num_4_out_6));  // open: dp
  num num_4 (
    .in_1(rs3), .out_8(num_4_out_8), .out_7(num_4_out_7), .out_6(num_4_out_6), .out_5(num_4_out_5),
    .out_4(num_4_out_4), .out_3(num_4_out_3), .out_2(num_4_out_2));
  _7_Segment_Display u_7_segment_display_8 (
    .g(num_5_out_5), .f(num_5_out_4), .a(num_5_out_3), .b(num_5_out_2), .e(num_5_out_8), .d(num_5_out_7),
    .c(num_5_out_6));  // open: dp
  num num_5 (
    .in_1(rt3), .out_8(num_5_out_8), .out_7(num_5_out_7), .out_6(num_5_out_6), .out_5(num_5_out_5),
    .out_4(num_5_out_4), .out_3(num_5_out_3), .out_2(num_5_out_2));
  _7_Segment_Display u_7_segment_display_9 (
    .g(num_6_out_5), .f(num_6_out_4), .a(num_6_out_3), .b(num_6_out_2), .e(num_6_out_8), .d(num_6_out_7),
    .c(num_6_out_6));  // open: dp
  num num_6 (
    .in_1(rd3), .out_8(num_6_out_8), .out_7(num_6_out_7), .out_6(num_6_out_6), .out_5(num_6_out_5),
    .out_4(num_6_out_4), .out_3(num_6_out_3), .out_2(num_6_out_2));
  _7_Segment_Display u_7_segment_display_10 (
    .g(num_7_out_5), .f(num_7_out_4), .a(num_7_out_3), .b(num_7_out_2), .e(num_7_out_8), .d(num_7_out_7),
    .c(num_7_out_6));  // open: dp
  num num_7 (
    .in_1(rs2), .out_8(num_7_out_8), .out_7(num_7_out_7), .out_6(num_7_out_6), .out_5(num_7_out_5),
    .out_4(num_7_out_4), .out_3(num_7_out_3), .out_2(num_7_out_2));
  _7_Segment_Display u_7_segment_display_11 (
    .g(num_8_out_5), .f(num_8_out_4), .a(num_8_out_3), .b(num_8_out_2), .e(num_8_out_8), .d(num_8_out_7),
    .c(num_8_out_6));  // open: dp
  num num_8 (
    .in_1(rt2), .out_8(num_8_out_8), .out_7(num_8_out_7), .out_6(num_8_out_6), .out_5(num_8_out_5),
    .out_4(num_8_out_4), .out_3(num_8_out_3), .out_2(num_8_out_2));
  _7_Segment_Display u_7_segment_display_12 (
    .g(num_9_out_5), .f(num_9_out_4), .a(num_9_out_3), .b(num_9_out_2), .e(num_9_out_8), .d(num_9_out_7),
    .c(num_9_out_6));  // open: dp
  num num_9 (
    .in_1(rd2), .out_8(num_9_out_8), .out_7(num_9_out_7), .out_6(num_9_out_6), .out_5(num_9_out_5),
    .out_4(num_9_out_4), .out_3(num_9_out_3), .out_2(num_9_out_2));
  _7_Segment_Display u_7_segment_display_13 (
    .g(num_10_out_5), .f(num_10_out_4), .a(num_10_out_3), .b(num_10_out_2), .e(num_10_out_8),
    .d(num_10_out_7), .c(num_10_out_6));  // open: dp
  num num_10 (
    .in_1(rs1), .out_8(num_10_out_8), .out_7(num_10_out_7), .out_6(num_10_out_6), .out_5(num_10_out_5),
    .out_4(num_10_out_4), .out_3(num_10_out_3), .out_2(num_10_out_2));
  _7_Segment_Display u_7_segment_display_14 (
    .g(num_11_out_5), .f(num_11_out_4), .a(num_11_out_3), .b(num_11_out_2), .e(num_11_out_8),
    .d(num_11_out_7), .c(num_11_out_6));  // open: dp
  num num_11 (
    .in_1(rt1), .out_8(num_11_out_8), .out_7(num_11_out_7), .out_6(num_11_out_6), .out_5(num_11_out_5),
    .out_4(num_11_out_4), .out_3(num_11_out_3), .out_2(num_11_out_2));
  _7_Segment_Display u_7_segment_display_15 (
    .g(num_12_out_5), .f(num_12_out_4), .a(num_12_out_3), .b(num_12_out_2), .e(num_12_out_8),
    .d(num_12_out_7), .c(num_12_out_6));  // open: dp
  num num_12 (
    .in_1(rd1), .out_8(num_12_out_8), .out_7(num_12_out_7), .out_6(num_12_out_6), .out_5(num_12_out_5),
    .out_4(num_12_out_4), .out_3(num_12_out_3), .out_2(num_12_out_2));
  _7_Segment_Display u_7_segment_display_16 (
    .g(num_13_out_5), .f(num_13_out_4), .a(num_13_out_3), .b(num_13_out_2), .e(num_13_out_8),
    .d(num_13_out_7), .c(num_13_out_6));  // open: dp
  num num_13 (
    .in_1(rs0), .out_8(num_13_out_8), .out_7(num_13_out_7), .out_6(num_13_out_6), .out_5(num_13_out_5),
    .out_4(num_13_out_4), .out_3(num_13_out_3), .out_2(num_13_out_2));
  _7_Segment_Display u_7_segment_display_17 (
    .g(num_14_out_5), .f(num_14_out_4), .a(num_14_out_3), .b(num_14_out_2), .e(num_14_out_8),
    .d(num_14_out_7), .c(num_14_out_6));  // open: dp
  num num_14 (
    .in_1(rt0), .out_8(num_14_out_8), .out_7(num_14_out_7), .out_6(num_14_out_6), .out_5(num_14_out_5),
    .out_4(num_14_out_4), .out_3(num_14_out_3), .out_2(num_14_out_2));
  _7_Segment_Display u_7_segment_display_18 (
    .g(num_15_out_5), .f(num_15_out_4), .a(num_15_out_3), .b(num_15_out_2), .e(num_15_out_8),
    .d(num_15_out_7), .c(num_15_out_6));  // open: dp
  num num_15 (
    .in_1(rd0), .out_8(num_15_out_8), .out_7(num_15_out_7), .out_6(num_15_out_6), .out_5(num_15_out_5),
    .out_4(num_15_out_4), .out_3(num_15_out_3), .out_2(num_15_out_2));
  Hex_Digit_Display hex_digit_display_1 (.value(addressJ[23:20]));  // open: dp
  Hex_Digit_Display hex_digit_display_2 (.value(bit_extender_5_out));  // open: dp
  assign bit_extender_5_out = {{2{1'b0}}, addressJ[25:24]};  // Bit_Extender bit_extender_5
  Hex_Digit_Display hex_digit_display_3 (.value(address[15:12]));  // open: dp
  Hex_Digit_Display hex_digit_display_4 (.value(addressJ[15:12]));  // open: dp
  Hex_Digit_Display hex_digit_display_5 (.value(addressJ[19:16]));  // open: dp
  Hex_Digit_Display hex_digit_display_6 (.value(address[11:8]));  // open: dp
  Hex_Digit_Display hex_digit_display_7 (.value(address[7:4]));  // open: dp
  Hex_Digit_Display hex_digit_display_8 (.value(addressJ[11:8]));  // open: dp
  Hex_Digit_Display hex_digit_display_9 (.value(addressJ[7:4]));  // open: dp
  Hex_Digit_Display hex_digit_display_10 (.value(address[3:0]));  // open: dp
  Hex_Digit_Display hex_digit_display_11 (.value(addressJ[3:0]));  // open: dp

  // Other names for the same wires on the sheet: ALUop[1:0] = out_2

  // Notes on the sheet:
  //   PC
  //   Operacion
  //   Instruction Memory
  //   Active Load
  //   Memoria 
  //   RS
  //   RT
  //   RD
  //   AddressJump:
  //   Address/offset:
endmodule

module PC (
  input  Clock,
  input  Reset,
  output [23:0] Address
);

  wire [23:0] adder_1_out;

  Adder #(.width(24)) adder_1 (.a(Address), .b(24'h1), .out(adder_1_out));  // open: cin, cout
  Register_part #(.width(24)) register_1 (.D(adder_1_out), .Q(Address), .clk(Clock), .clr(Reset));  // open: en
endmodule

module Decode (
  input  [31:0] in_1,
  output [25:0] Address_J,
  output [15:0] Address,
  output [4:0] rs,
  output [4:0] rt,
  output [4:0] rd,
  output [4:0] Shamt,
  output [5:0] Dibujado,
  output [5:0] funct,
  output [5:0] Op
);

  wire not_1_out;
  wire [1:0] comparator_2_eq;
  wire [25:0] demultiplexer_1_out0;
  wire [25:16] demultiplexer_1_out1;

  Comparator #(.width(6)) comparator_1 (.a(in_1[31:26]), .b({6{1'b0}}), .eq(comparator_2_eq[1]));  // open: gt, lt
  Demultiplexer #(.width(26), .enable("false")) demultiplexer_1 (
    .out0(demultiplexer_1_out0), .out1({demultiplexer_1_out1, rd, Shamt, funct}), .in(in_1[25:0]),
    .sel(comparator_2_eq[1]));
  Comparator #(.width(6)) comparator_2 (.a(in_1[31:26]), .b(6'b000010), .eq(comparator_2_eq[0]));  // open: gt, lt
  Multiplexer #(.width(6), .enable("false")) multiplexer_1 (
    .in0(funct), .in1(in_1[31:26]), .out(Dibujado), .sel(not_1_out));
  not not_1 (not_1_out, comparator_2_eq[1]);
  Multiplexer #(.width(16), .enable("false")) multiplexer_2 (
    .in0(demultiplexer_1_out0[15:0]), .in1({16{1'b0}}), .out(Address), .sel(comparator_2_eq[0]));
  Multiplexer #(.width(26), .enable("false")) multiplexer_3 (
    .in0({26{1'b0}}), .in1(demultiplexer_1_out0), .out(Address_J), .sel(comparator_2_eq[0]));
  Multiplexer #(.select(2), .width(10), .enable("false")) multiplexer_4 (
    .in0(demultiplexer_1_out0[25:16]), .in1({10{1'b0}}), .in2(demultiplexer_1_out1), .out({rs, rt}),
    .sel(comparator_2_eq));  // open: in3

  assign Op = in_1[31:26];
endmodule

module Penilla (
  input  [4:0] Input,
  output s0,
  output s1,
  output s2,
  output s3,
  output s4
);


  assign s0 = Input[0];
  assign s1 = Input[1];
  assign s2 = Input[2];
  assign s3 = Input[3];
  assign s4 = Input[4];
endmodule

module num (
  input  in_1,
  output out_2,
  output out_3,
  output out_4,
  output out_5,
  output out_6,
  output out_7,
  output out_8
);

  Multiplexer #(.width(7), .enable("false")) multiplexer_1 (
    .in0(7'b1110111), .in1(7'b0010001), .out({out_8, out_7, out_6, out_5, out_4, out_3, out_2}), .sel(in_1));
endmodule

// Show
module ShowOp_funct (
  input  [5:0] Funct_0p,
  output [6:0] s1,
  output [6:0] s2,
  output [6:0] s2_2
);

  wire comparator_1_eq, comparator_2_eq, comparator_3_eq, comparator_4_eq, comparator_5_eq, comparator_6_eq,
       comparator_7_eq, comparator_8_eq, comparator_9_eq, comparator_10_eq, letter_1_out_2, letter_1_out_3,
       letter_1_out_4, letter_1_out_5, letter_1_out_6, letter_1_out_7, letter_1_out_8, letter_2_out_2,
       letter_2_out_3, letter_2_out_4, letter_2_out_5, letter_2_out_6, letter_2_out_7, letter_2_out_8,
       letter_3_out_2, letter_3_out_3, letter_3_out_4, letter_3_out_5, letter_3_out_6, letter_3_out_7,
       letter_3_out_8;
  wire [3:0] opchooser_1_s0;

  Comparator #(.width(6)) comparator_1 (.a(Funct_0p), .b(6'b100000), .eq(comparator_1_eq));  // open: gt, lt
  Comparator #(.width(6)) comparator_2 (.a(Funct_0p), .b(6'b100010), .eq(comparator_2_eq));  // open: gt, lt
  Comparator #(.width(6)) comparator_3 (.a(Funct_0p), .b(6'b100100), .eq(comparator_3_eq));  // open: gt, lt
  Comparator #(.width(6)) comparator_4 (.a(Funct_0p), .b(6'b100101), .eq(comparator_4_eq));  // open: gt, lt
  Comparator #(.width(6)) comparator_5 (.a(Funct_0p), .b(6'b011000), .eq(comparator_5_eq));  // open: gt, lt
  Comparator #(.width(6)) comparator_6 (.a(Funct_0p), .b(6'b000100), .eq(comparator_6_eq));  // open: gt, lt
  Comparator #(.width(6)) comparator_7 (.a(Funct_0p), .b(6'b000010), .eq(comparator_7_eq));  // open: gt, lt
  Comparator #(.width(6)) comparator_8 (.a(Funct_0p), .b(6'b100011), .eq(comparator_8_eq));  // open: gt, lt
  Comparator #(.width(6)) comparator_9 (.a(Funct_0p), .b(6'b101011), .eq(comparator_9_eq));  // open: gt, lt
  Comparator #(.width(6)) comparator_10 (.a(Funct_0p), .b(6'b001000), .eq(comparator_10_eq));  // open: gt, lt
  OpChooser opchooser_1 (
    .add(comparator_1_eq), .sub(comparator_2_eq), .\and (comparator_3_eq), .\or (comparator_4_eq),
    .mult(comparator_5_eq), .beq(comparator_6_eq), .jump(comparator_7_eq), .load(comparator_8_eq),
    .store(comparator_9_eq), .addi(comparator_10_eq), .s3(opchooser_1_s0[3]), .s2(opchooser_1_s0[2]),
    .s1(opchooser_1_s0[1]), .s0(opchooser_1_s0[0]));
  Multiplexer #(.select(4), .width(21), .enable("false")) multiplexer_1 (
    .in0(21'h20408), .in1(21'h1e7cdf), .in2(21'h1f3abe), .in3(21'h1e6bdf), .in4(21'h133b88),
    .in5(21'h113ad7), .in6(21'h7f7fc), .in7(21'h15faf1), .in8(21'h1d7ae4), .in9(21'h1d7abe),
    .in10(21'h113cdf), .out({s2_2, s2, s1}), .sel(opchooser_1_s0));  // open: in11, in12, in13, in14, in15
  _7_Segment_Display u_7_segment_display_1 (
    .g(letter_1_out_5), .f(letter_1_out_4), .a(letter_1_out_3), .b(letter_1_out_2), .e(letter_1_out_8),
    .d(letter_1_out_7), .c(letter_1_out_6));  // open: dp
  Letter letter_1 (
    .Number(s1), .out_8(letter_1_out_8), .out_7(letter_1_out_7), .out_6(letter_1_out_6),
    .out_5(letter_1_out_5), .out_4(letter_1_out_4), .out_3(letter_1_out_3), .out_2(letter_1_out_2));
  _7_Segment_Display u_7_segment_display_2 (
    .g(letter_2_out_5), .f(letter_2_out_4), .a(letter_2_out_3), .b(letter_2_out_2), .e(letter_2_out_8),
    .d(letter_2_out_7), .c(letter_2_out_6));  // open: dp
  Letter letter_2 (
    .Number(s2), .out_8(letter_2_out_8), .out_7(letter_2_out_7), .out_6(letter_2_out_6),
    .out_5(letter_2_out_5), .out_4(letter_2_out_4), .out_3(letter_2_out_3), .out_2(letter_2_out_2));
  _7_Segment_Display u_7_segment_display_3 (
    .g(letter_3_out_5), .f(letter_3_out_4), .a(letter_3_out_3), .b(letter_3_out_2), .e(letter_3_out_8),
    .d(letter_3_out_7), .c(letter_3_out_6));  // open: dp
  Letter letter_3 (
    .Number(s2_2), .out_8(letter_3_out_8), .out_7(letter_3_out_7), .out_6(letter_3_out_6),
    .out_5(letter_3_out_5), .out_4(letter_3_out_4), .out_3(letter_3_out_3), .out_2(letter_3_out_2));

  // Other names for the same wires on the sheet: s3[6:0] = s2_2

  // Notes on the sheet:
  //   Add
  //   Sub
  //   And
  //   or
  //   Mult
  //   Beq
  //   jum
  //   load
  //   store
  //   addi
endmodule

module Letter (
  input  [6:0] Number,
  output out_2,
  output out_3,
  output out_4,
  output out_5,
  output out_6,
  output out_7,
  output out_8
);


  assign out_2 = Number[0];
  assign out_3 = Number[1];
  assign out_4 = Number[2];
  assign out_5 = Number[3];
  assign out_6 = Number[4];
  assign out_7 = Number[5];
  assign out_8 = Number[6];
endmodule

module OpChooser (
  input  add,
  input  sub,
  input  \and ,
  input  \or ,
  input  mult,
  input  beq,
  input  jump,
  input  load,
  input  store,
  input  addi,
  output s3,
  output s2,
  output s1,
  output s0
);

  or or_1 (s3, addi, store, load);
  or or_2 (s2, jump, beq, mult, \or );
  or or_3 (s1, addi, jump, beq, \and , sub);
  or or_4 (s0, store, jump, mult, \and , add);
endmodule

module Register (
  input  Clock,
  input  Reset,
  input  [4:0] ReadRegister1,
  input  [31:0] WriteData,
  input  RegWrite,
  input  [4:0] ReadRegister2,
  input  [4:0] WriteRegister,
  output [31:0] ReadData1,
  output [31:0] ReadData2
);

  wire r0, r1, r2, r3, r4, r5, r6, r7, r8, r9, r10, r11, r12, r13, r14, r15, r16, r17, r18, r19, r20, r21,
       r22, r23, r24, r25, r26, r27, r28, r29, r30, r31;
  wire [31:0] i0, i1, i2, i3, i4, i5, i6, i7, i8, i9, i10, i11, i12, i13, i14, i15, i16, i17, i18, i19, i20,
       i21, i22, i23, i24, i25, i26, i27, i28, i29, i30, i31, o0, o1, o2, o3, o4, o5, o6, o7, o8, o9, o10,
       o11, o12, o13, o14, o15, o16, o17, o18, o19, o20, o21, o22, o23, o24, o25, o26, o27, o28, o29, o30,
       o31;

  Multiplexer #(.select(5), .width(32), .enable("false")) multiplexer_1 (
    .in0(o0), .in1(o1), .in2(o2), .in3(o3), .in4(o4), .in5(o5), .in6(o6), .in7(o7), .in8(o8), .in9(o9),
    .in10(o10), .in11(o11), .in12(o12), .in13(o13), .in14(o14), .in15(o15), .in16(o16), .in17(o17),
    .in18(o18), .in19(o19), .in20(o20), .in21(o21), .in22(o22), .in23(o23), .in24(o24), .in25(o25),
    .in26(o26), .in27(o27), .in28(o28), .in29(o29), .in30(o30), .in31(o31), .out(ReadData1),
    .sel(ReadRegister1));
  Multiplexer #(.select(5), .width(32), .enable("false")) multiplexer_2 (
    .in0(o0), .in1(o1), .in2(o2), .in3(o3), .in4(o4), .in5(o5), .in6(o6), .in7(o7), .in8(o8), .in9(o9),
    .in10(o10), .in11(o11), .in12(o12), .in13(o13), .in14(o14), .in15(o15), .in16(o16), .in17(o17),
    .in18(o18), .in19(o19), .in20(o20), .in21(o21), .in22(o22), .in23(o23), .in24(o24), .in25(o25),
    .in26(o26), .in27(o27), .in28(o28), .in29(o29), .in30(o30), .in31(o31), .out(ReadData2),
    .sel(ReadRegister2));
  Register_part #(.width(32)) register_1 (.D(i0), .en(r0), .Q(o0), .clk(Clock), .clr(Reset));
  Register_part #(.width(32)) register_2 (.D(i8), .en(r8), .Q(o8), .clk(Clock), .clr(Reset));
  Register_part #(.width(32)) register_3 (.D(i16), .en(r16), .Q(o16), .clk(Clock), .clr(Reset));
  Register_part #(.width(32)) register_4 (.D(i24), .en(r24), .Q(o24), .clk(Clock), .clr(Reset));
  Demultiplexer #(.select(5), .width(32), .enable("false")) demultiplexer_1 (
    .out0(i0), .out1(i1), .out2(i2), .out3(i3), .out4(i4), .out5(i5), .out6(i6), .out7(i7), .out8(i8),
    .out9(i9), .out10(i10), .out11(i11), .out12(i12), .out13(i13), .out14(i14), .out15(i15), .out16(i16),
    .out17(i17), .out18(i18), .out19(i19), .out20(i20), .out21(i21), .out22(i22), .out23(i23), .out24(i24),
    .out25(i25), .out26(i26), .out27(i27), .out28(i28), .out29(i29), .out30(i30), .out31(i31),
    .in(WriteData), .sel(WriteRegister));
  Register_part #(.width(32)) register_5 (.D(i1), .en(r1), .Q(o1), .clk(Clock), .clr(Reset));
  Register_part #(.width(32)) register_6 (.D(i9), .en(r9), .Q(o9), .clk(Clock), .clr(Reset));
  Register_part #(.width(32)) register_7 (.D(i17), .en(r17), .Q(o17), .clk(Clock), .clr(Reset));
  Register_part #(.width(32)) register_8 (.D(i25), .en(r25), .Q(o25), .clk(Clock), .clr(Reset));
  Register_part #(.width(32)) register_9 (.D(i2), .en(r2), .Q(o2), .clk(Clock), .clr(Reset));
  Register_part #(.width(32)) register_10 (.D(i10), .en(r10), .Q(o10), .clk(Clock), .clr(Reset));
  Register_part #(.width(32)) register_11 (.D(i18), .en(r18), .Q(o18), .clk(Clock), .clr(Reset));
  Register_part #(.width(32)) register_12 (.D(i26), .en(r26), .Q(o26), .clk(Clock), .clr(Reset));
  Demultiplexer #(.select(5), .enable("false")) demultiplexer_2 (
    .out0(r0), .out1(r1), .out2(r2), .out3(r3), .out4(r4), .out5(r5), .out6(r6), .out7(r7), .out8(r8),
    .out9(r9), .out10(r10), .out11(r11), .out12(r12), .out13(r13), .out14(r14), .out15(r15), .out16(r16),
    .out17(r17), .out18(r18), .out19(r19), .out20(r20), .out21(r21), .out22(r22), .out23(r23), .out24(r24),
    .out25(r25), .out26(r26), .out27(r27), .out28(r28), .out29(r29), .out30(r30), .out31(r31), .in(RegWrite),
    .sel(WriteRegister));
  Register_part #(.width(32)) register_13 (.D(i3), .en(r3), .Q(o3), .clk(Clock), .clr(Reset));
  Register_part #(.width(32)) register_14 (.D(i11), .en(r11), .Q(o11), .clk(Clock), .clr(Reset));
  Register_part #(.width(32)) register_15 (.D(i19), .en(r19), .Q(o19), .clk(Clock), .clr(Reset));
  Register_part #(.width(32)) register_16 (.D(i27), .en(r27), .Q(o27), .clk(Clock), .clr(Reset));
  Register_part #(.width(32)) register_17 (.D(i4), .en(r4), .Q(o4), .clk(Clock), .clr(Reset));
  Register_part #(.width(32)) register_18 (.D(i12), .en(r12), .Q(o12), .clk(Clock), .clr(Reset));
  Register_part #(.width(32)) register_19 (.D(i20), .en(r20), .Q(o20), .clk(Clock), .clr(Reset));
  Register_part #(.width(32)) register_20 (.D(i28), .en(r28), .Q(o28), .clk(Clock), .clr(Reset));
  Register_part #(.width(32)) register_21 (.D(i5), .en(r5), .Q(o5), .clk(Clock), .clr(Reset));
  Register_part #(.width(32)) register_22 (.D(i13), .en(r13), .Q(o13), .clk(Clock), .clr(Reset));
  Register_part #(.width(32)) register_23 (.D(i21), .en(r21), .Q(o21), .clk(Clock), .clr(Reset));
  Register_part #(.width(32)) register_24 (.D(i29), .en(r29), .Q(o29), .clk(Clock), .clr(Reset));
  Register_part #(.width(32)) register_25 (.D(i6), .en(r6), .Q(o6), .clk(Clock), .clr(Reset));
  Register_part #(.width(32)) register_26 (.D(i14), .en(r14), .Q(o14), .clk(Clock), .clr(Reset));
  Register_part #(.width(32)) register_27 (.D(i22), .en(r22), .Q(o22), .clk(Clock), .clr(Reset));
  Register_part #(.width(32)) register_28 (.D(i30), .en(r30), .Q(o30), .clk(Clock), .clr(Reset));
  Register_part #(.width(32)) register_29 (.D(i7), .en(r7), .Q(o7), .clk(Clock), .clr(Reset));
  Register_part #(.width(32)) register_30 (.D(i15), .en(r15), .Q(o15), .clk(Clock), .clr(Reset));
  Register_part #(.width(32)) register_31 (.D(i23), .en(r23), .Q(o23), .clk(Clock), .clr(Reset));
  Register_part #(.width(32)) register_32 (.D(i31), .en(r31), .Q(o31), .clk(Clock), .clr(Reset));
endmodule

module preRegister (
  input  [31:0] \input ,
  input  [31:0] saved,
  output [31:0] \output 
);

  wire comparator_1_eq;

  Comparator #(.width(32)) comparator_1 (.a({32{1'b0}}), .b(\input ), .eq(comparator_1_eq));  // open: gt, lt
  Multiplexer #(.width(32), .enable("false")) multiplexer_1 (
    .in0(\input ), .in1(saved), .out(\output ), .sel(comparator_1_eq));
endmodule

module TestCircuit (
  input  in_1,
  input  in_2,
  output out_3,
  output out_4
);

  wire clock_1_out, comparator_1_eq, comparator_2_eq, demultiplexer_1_out0, demultiplexer_1_out1,
       multiplexer_1_out;

  Demultiplexer #(.enable("false")) demultiplexer_1 (
    .out0(demultiplexer_1_out0), .out1(demultiplexer_1_out1), .in(in_1), .sel(in_2));
  Clock clock_1 (.out(clock_1_out));
  Register_part #(.width(1)) register_1 (
    .D(demultiplexer_1_out1), .Q(out_4), .clk(clock_1_out), .clr(comparator_1_eq));  // open: en
  Comparator #(.width(1)) comparator_1 (.a(in_1), .b(1'b0), .eq(comparator_1_eq));  // open: gt, lt
  Register_part #(.width(1)) register_2 (
    .D(multiplexer_1_out), .Q(out_3), .clk(clock_1_out), .clr(comparator_1_eq));  // open: en
  Comparator #(.width(1)) comparator_2 (.a(1'b0), .b(demultiplexer_1_out0), .eq(comparator_2_eq));  // open: gt, lt
  Multiplexer #(.enable("false")) multiplexer_1 (
    .in0(demultiplexer_1_out0), .in1(out_3), .out(multiplexer_1_out), .sel(comparator_2_eq));
endmodule

module ALU (
  input  [31:0] Dato1,
  input  [31:0] Dato2,
  input  [3:0] ALUop,
  output [31:0] ALUResult,
  output Zero
);

  wire comparator_1_eq, comparator_2_eq, comparator_3_eq, comparator_4_eq, comparator_5_eq;
  wire [2:0] Selector;
  wire [31:0] Add, And, Mult, Or, Sub;

  Comparator #(.width(4)) comparator_1 (.a(ALUop), .b(4'b0010), .eq(comparator_1_eq));  // open: gt, lt
  Comparator #(.width(4)) comparator_2 (.a(ALUop), .b(4'b0110), .eq(comparator_2_eq));  // open: gt, lt
  Comparator #(.width(4)) comparator_3 (.a(ALUop), .b(4'b0000), .eq(comparator_3_eq));  // open: gt, lt
  Comparator #(.width(4)) comparator_4 (.a(ALUop), .b(4'b0001), .eq(comparator_4_eq));  // open: gt, lt
  Comparator #(.width(4)) comparator_5 (.a(ALUop), .b(4'b1000), .eq(comparator_5_eq));  // open: gt, lt
  Multiplexer #(.width(3)) multiplexer_1 (
    .in0(3'b000), .in1(3'b000), .out(Selector), .sel(comparator_1_eq), .en(comparator_1_eq));
  Multiplexer #(.width(3)) multiplexer_2 (
    .in0(3'b000), .in1(3'b001), .out(Selector), .sel(comparator_2_eq), .en(comparator_2_eq));
  Multiplexer #(.width(3)) multiplexer_3 (
    .in0(3'b000), .in1(3'b010), .out(Selector), .sel(comparator_3_eq), .en(comparator_3_eq));
  Multiplexer #(.width(3)) multiplexer_4 (
    .in0(3'b000), .in1(3'b011), .out(Selector), .sel(comparator_4_eq), .en(comparator_4_eq));
  Multiplexer #(.width(3)) multiplexer_5 (
    .in0(3'b000), .in1(3'b100), .out(Selector), .sel(comparator_5_eq), .en(comparator_5_eq));
  Multiplexer #(.select(3), .width(32), .enable("false")) multiplexer_6 (
    .in0(Add), .in1(Sub), .in2(And), .in3(Or), .in4(Mult), .out(ALUResult), .sel(Selector));  // open: in5, in6, in7
  Adder #(.width(32)) adder_1 (.a(Dato1), .b(Dato2), .out(Add));  // open: cin, cout
  Subtractor #(.width(32)) subtractor_1 (.a(Dato1), .b(Dato2), .out(Sub));  // open: bin, bout
  assign And = Dato1 & Dato2;  // AND_Gate and_1, 32 bits wide
  assign Or = Dato1 | Dato2;  // OR_Gate or_1, 32 bits wide
  Multiplier #(.width(32)) multiplier_1 (.a(Dato1), .b(Dato2), .out(Mult));  // open: cin, cout
  Comparator #(.width(32)) comparator_6 (.a(ALUResult), .b({32{1'b0}}), .eq(Zero));  // open: gt, lt

  // Notes on the sheet:
  //   Add
  //   Subtract
  //   AND
  //   OR
  //   Mult
endmodule

module Unidad_de_Control (
  input  [5:0] OpCode,
  output RegDst,
  output ALUSrc,
  output MemToReg,
  output Regwrite,
  output MemRead,
  output MemWrite,
  output Branch,
  output [1:0] ALUop,
  output Jump
);

  wire comparator_1_eq, comparator_2_eq, comparator_3_eq, comparator_4_eq, comparator_6_eq;
  wire [2:0] selector;

  Comparator #(.width(6)) comparator_1 (.a(OpCode), .b(6'b100011), .eq(comparator_1_eq));  // open: gt, lt
  Comparator #(.width(6)) comparator_2 (.a(OpCode), .b(6'b101011), .eq(comparator_2_eq));  // open: gt, lt
  Comparator #(.width(6)) comparator_3 (.a(OpCode), .b(6'b000100), .eq(comparator_3_eq));  // open: gt, lt
  Comparator #(.width(6)) comparator_4 (.a(OpCode), .b({6{1'b0}}), .eq(comparator_4_eq));  // open: gt, lt
  Comparator #(.width(6)) comparator_5 (.a(OpCode), .b(6'b000010), .eq(Jump));  // open: gt, lt
  Comparator #(.width(6)) comparator_6 (.a(OpCode), .b(6'b001000), .eq(comparator_6_eq));  // open: gt, lt
  Multiplexer #(.width(3)) multiplexer_1 (
    .in0(3'b000), .in1(3'b001), .out(selector), .sel(comparator_1_eq), .en(comparator_1_eq));
  Multiplexer #(.width(3)) multiplexer_2 (
    .in0(3'b000), .in1(3'b010), .out(selector), .sel(comparator_2_eq), .en(comparator_2_eq));
  Multiplexer #(.width(3)) multiplexer_3 (
    .in0(3'b000), .in1(3'b011), .out(selector), .sel(comparator_3_eq), .en(comparator_3_eq));
  Multiplexer #(.width(3)) multiplexer_4 (
    .in0(3'b000), .in1(3'b000), .out(selector), .sel(comparator_4_eq), .en(comparator_4_eq));
  Multiplexer #(.width(3)) multiplexer_5 (.in0(3'b000), .in1(3'b000), .out(selector), .sel(Jump), .en(Jump));
  Multiplexer #(.width(3)) multiplexer_6 (
    .in0(3'b000), .in1(3'b100), .out(selector), .sel(comparator_6_eq), .en(comparator_6_eq));
  Multiplexer #(.select(3), .width(9), .enable("false")) multiplexer_7 (
    .in0(9'h122), .in1(9'hf0), .in2(9'h88), .in3(9'h5), .in4(9'ha2),
    .out({RegDst, ALUSrc, MemToReg, Regwrite, MemRead, MemWrite, Branch, ALUop}), .sel(selector));  // open: in5, in6, in7

  // Notes on the sheet:
  //   Typo R
  //   LW
  //   SW
  //   Branch
  //   Jump
  //   LW
  //   SW
  //   Branch
  //   Typo R
  //   Jump
  //   Addi
  //   0 for rd and 1 for rt
endmodule

module ALU_Control (
  input  [1:0] ALUop,
  input  [5:0] funct,
  output [3:0] AluControlOutput
);

  wire comparator_1_eq, comparator_2_eq, comparator_3_eq, comparator_4_eq, comparator_5_eq, comparator_6_eq,
       comparator_7_eq, comparator_8_eq, ControlDesicion;
  wire [3:0] ALUSignal, FunSignal;

  Comparator #(.width(1)) comparator_1 (.a(ALUop[0]), .b(1'b1), .eq(comparator_1_eq));  // open: gt, lt
  Comparator #(.width(2)) comparator_2 (.a(ALUop), .b(2'b00), .eq(comparator_2_eq));  // open: gt, lt
  Comparator #(.width(4)) comparator_3 (.a(funct[3:0]), .b(4'b0000), .eq(comparator_3_eq));  // open: gt, lt
  Comparator #(.width(4)) comparator_4 (.a(funct[3:0]), .b(4'b0010), .eq(comparator_4_eq));  // open: gt, lt
  Comparator #(.width(4)) comparator_5 (.a(funct[3:0]), .b(4'b0100), .eq(comparator_5_eq));  // open: gt, lt
  Comparator #(.width(4)) comparator_6 (.a(funct[3:0]), .b(4'b0101), .eq(comparator_6_eq));  // open: gt, lt
  Comparator #(.width(4)) comparator_7 (.a(funct[3:0]), .b(4'b1010), .eq(comparator_7_eq));  // open: gt, lt
  Comparator #(.width(4)) comparator_8 (.a(funct[3:0]), .b(4'b1000), .eq(comparator_8_eq));  // open: gt, lt
  Multiplexer #(.width(4)) multiplexer_1 (
    .in0(4'b0000), .in1(4'b0110), .out(ALUSignal), .sel(comparator_1_eq), .en(comparator_1_eq));
  or or_1 (ControlDesicion, comparator_1_eq, comparator_2_eq);
  Multiplexer #(.width(4)) multiplexer_2 (
    .in0(4'b0000), .in1(4'b0010), .out(ALUSignal), .sel(comparator_2_eq), .en(comparator_2_eq));
  Multiplexer #(.width(4)) multiplexer_3 (
    .in0(4'b0000), .in1(4'b0010), .out(FunSignal), .sel(comparator_3_eq), .en(comparator_3_eq));
  Multiplexer #(.width(4)) multiplexer_4 (
    .in0(4'b0000), .in1(4'b0110), .out(FunSignal), .sel(comparator_4_eq), .en(comparator_4_eq));
  Multiplexer #(.width(4)) multiplexer_5 (
    .in0(4'b0000), .in1(4'b0000), .out(FunSignal), .sel(comparator_5_eq), .en(comparator_5_eq));
  Multiplexer #(.width(4)) multiplexer_6 (
    .in0(4'b0000), .in1(4'b0001), .out(FunSignal), .sel(comparator_6_eq), .en(comparator_6_eq));
  Multiplexer #(.width(4)) multiplexer_7 (
    .in0(4'b0000), .in1(4'b0111), .out(FunSignal), .sel(comparator_7_eq), .en(comparator_7_eq));
  Multiplexer #(.width(4)) multiplexer_8 (
    .in0(4'b0000), .in1(4'b1000), .out(FunSignal), .sel(comparator_8_eq), .en(comparator_8_eq));
  Multiplexer #(.width(4), .enable("false")) multiplexer_9 (
    .in0(FunSignal), .in1(ALUSignal), .out(AluControlOutput), .sel(ControlDesicion));
endmodule

module test (
  input  [3:0] in_1,
  input  in_2,
  output [3:0] out_3
);

  wire clock_1_out;

  Clock clock_1 (.out(clock_1_out));
  Register_part #(.width(4)) register_1 (.D(in_1), .en(in_2), .Q(out_3), .clk(clock_1_out));  // open: clr
endmodule
